# Fritzing sketch Electrical System Layout (saved by Fritzing 0.9.3b)
perfboards: 1

parts:
  ATmega17 = ATmega16 [chip_label=ATmega16 package="DIP (Dual Inline) [THT]"]
  Programmer1 = female pin header, 6 pins [form="♀ (female)"]
  BT1 = female pin header, 4 pins [form="♀ (female)"]
  Power1 = Screw terminal - 2 pins [package=THT]
  Motor_3 = Screw terminal - 2 pins [package=THT]
  Motor_4 = Screw terminal - 2 pins [package=THT]
  Power_plug1 = Power plug
  Power2 = Screw terminal - 2 pins [package=THT]
  H1 = HC-05
  L298N1 = L298N
  M1 = DC Motor
  M2 = DC Motor

nets:
  N1: ATmega17.1, Motor_4.pin2
  N2: ATmega17.2, Motor_4.pin1
  N3: ATmega17.3, Motor_3.pin2
  N4: ATmega17.4, Motor_3.pin1
  N5: ATmega17.6, Programmer1.pin1
  N6: ATmega17.7, Programmer1.pin2
  N7: ATmega17.8, Programmer1.pin3
  N8: ATmega17.9, Programmer1.pin4
  N9: ATmega17.10, Programmer1.pin5, BT1.pin1, Power1.pin2, H1.VCC
  GND: ATmega17.11, Programmer1.pin6, BT1.pin2, Power1.pin1, Power_plug1.GND, Power2.pin2, H1.GND
  N10: ATmega17.14, BT1.pin3, H1.TXD
  N11: ATmega17.15, BT1.pin4, H1.RXD
  N12: Power_plug1.VCC, Power2.pin1
  N13: L298N1.OUT1, M2.pin_2
  N14: L298N1.OUT2, M2.pin_1
  N15: L298N1.OUT3, M1.pin_2
  N16: L298N1.OUT4, M1.pin_1
  N17: L298N1.5V#9, L298N1.ENA
  N18: L298N1.5V#10, L298N1.ENB

custom parts:
  HC-05: HC-05 is a Bluetooth Module
  L298N: L298N Motor Driver (max rating: 46V, 2A) Set 5V Enable jumper to enable 5V regultor (needed for the L298N IC) and get +5V output at screw terminal [or] supply external +5V at screw terminal Set ENA and/or ENB to +5V to enable motor permanently [or] supply ENA and/or ENB with PWM signal IN1 and IN2 set rotation direction for motor A (OUT1/OUT2) IN2 and IN3 set rotation direction for motor B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
